// Logisim project Parity.circ as structural Verilog: 1 circuit, main circuit main
module main (
);

  wire and_1_out, and_2_out, and_3_out, and_4_out, and_5_out, and_6_out, and_7_out, and_8_out, and_9_out,
       and_10_out, and_12_out, and_13_out, and_14_out, and_15_out, and_16_out, and_17_out, and_18_out,
       dipswitch_1_p2, dipswitch_1_p3, dipswitch_2_p2, dipswitch_2_p3, or_1_out, or_2_out, or_3_out,
       or_4_out, or_5_out, or_6_out, or_7_out, pull_resistor_1_node, pull_resistor_2_node;

  Pull_Resistor pull_resistor_1 (.node(pull_resistor_1_node));
  // DipSwitch dipswitch_1: pin names not known; wires that end beside it: pull_resistor_1_node, dipswitch_1_p2, dipswitch_1_p3, dipswitch_1_p2, dipswitch_1_p3
  Pull_Resistor pull_resistor_2 (.node(pull_resistor_2_node));
  // DipSwitch dipswitch_2: pin names not known; wires that end beside it: pull_resistor_2_node, dipswitch_2_p2, dipswitch_2_p3, dipswitch_2_p2, dipswitch_2_p3
  Pull_Resistor pull_resistor_3 (.node(dipswitch_1_p2));
  Pull_Resistor pull_resistor_4 (.node(dipswitch_1_p3));
  Pull_Resistor pull_resistor_5 (.node(dipswitch_2_p2));
  Pull_Resistor pull_resistor_6 (.node(dipswitch_2_p3));
  and and_1 (and_1_out, ~pull_resistor_1_node, ~dipswitch_1_p3);  // AND_Gate
  and and_2 (and_2_out, ~pull_resistor_2_node, ~dipswitch_2_p3);  // AND_Gate
  and and_3 (and_3_out, ~dipswitch_1_p2, ~dipswitch_1_p3);  // AND_Gate
  and and_4 (and_4_out, ~dipswitch_2_p2, ~dipswitch_2_p3);  // AND_Gate
  and and_5 (and_5_out, pull_resistor_1_node, and_3_out);
  and and_6 (and_6_out, dipswitch_1_p2, and_1_out);
  and and_7 (and_7_out, pull_resistor_2_node, and_4_out);
  and and_8 (and_8_out, dipswitch_2_p2, and_2_out);
  and and_9 (and_9_out, dipswitch_1_p2, dipswitch_1_p3);
  and and_10 (and_10_out, dipswitch_2_p2, dipswitch_2_p3);
  or or_1 (or_1_out, and_5_out, and_6_out);
  and and_11 (pull_resistor_1_node, pull_resistor_1_node, and_9_out);
  or or_2 (or_2_out, and_7_out, and_8_out);
  and and_12 (and_12_out, pull_resistor_2_node, and_10_out);
  or or_3 (or_3_out, or_1_out, pull_resistor_1_node);
  and and_13 (and_13_out, ~dipswitch_1_p2, ~dipswitch_1_p3);  // AND_Gate
  or or_4 (or_4_out, or_2_out, and_12_out);
  and and_14 (and_14_out, ~dipswitch_2_p2, dipswitch_2_p2);  // AND_Gate
  and and_15 (and_15_out, ~pull_resistor_1_node, and_13_out);  // AND_Gate
  and and_16 (and_16_out, ~pull_resistor_2_node, and_14_out);  // AND_Gate
  or or_5 (or_5_out, or_3_out, and_15_out);
  LED led_1 (.in(1'b0));
  or or_6 (or_6_out, or_4_out, and_16_out);
  LED led_2 (.in(or_6_out));
  and and_17 (and_17_out, or_5_out, ~or_6_out);  // AND_Gate
  and and_18 (and_18_out, ~or_5_out, or_6_out);  // AND_Gate
  or or_7 (or_7_out, and_17_out, and_18_out);
  LED led_3 (.in(or_7_out));

  // Notes on the sheet:
  //   A
  //   C
  //   Z2
  //   Z0
  //   B = Y_1 = B'
  //   C = Y_0= A'B'+BC
  //   B
  //   C
  //   B = Z_1 = B'
  //   C = Z_0 = B'C+A;B
  //   Z1
  //   Z0
  //   A = Y_2 = AC' + B'C' + A'BC
  //   A
  //   B
  //   A = Z_2 = AC'+BC'+A'B'C
  //   Z2
  //   Z1
  //   B
  //   C
  //   Z1
  //   Z0
  //   A
  //   Z2
  //   Forward S-box Parity Generator
  //   B
  //   C
  //   Inverse S-box Parity Checker
  //   Z1
  //   Z0
  //   A
  //   Z2
  //   P_OUT = AB'C'+A'BC'+ABC+A'B'C
  //   P_BACK = Z2Z1'Z0'+Z2'Z1Z0'+Z2Z1Z0+Z2'Z1'Z0
  //   P_OUT
  //   P_BACK
  //   P_OUT
  //   P_BACK
  //   Error Detection
  //   ERROR = (P_OUT)(P_BACK)' + (P_OUT)'(P_BACK)
endmodule
